# Fritzing sketch fritzing (saved by Fritzing 0.9.6b)
breadboards: 1

parts:
  Part1 = Arduino Uno (Rev3)
  R1 = Resistor [tolerance=±5% power=0.25 resistance=220 package=THT]
  R2 = Photocell (LDR) [package=THT]
  KY-1 = Keyes Relay [package=THT]
  LED1 = LEDs [package=led10mm]
  Part2 = Lilypad Battery Connect

nets (from the breadboard view):
  N1: Part1.A0, R1.Pin_1, R2.pin_0
  N2: Part1.D2, KY-1.signal
  N3: Part1.5V, R2.pin_1, KY-1.power
  N4: Part1.GND, R1.Pin_0, KY-1.ground
  N5: KY-1.NC, Part2.-
  N6: KY-1.C, LED1.C
  N7: LED1.A, Part2.+

notes:
  AC 220V

custom parts:
  Keyes Relay: The Keyes 5V relay module is suitable for SCM development, home appliance control. It uses a 5V~12V TIL control signal which can control DC / AC signal.
  LEDs: LEDs Standard schematic elements and footprints for 5mm, 3mm, 1206, and 0603 sized LEDs. 5mm - Spark Fun Electronics SKU : COM-00529 (and others)
